// Logisim project COMPONENTE01.circ as structural Verilog: 1 circuit, main circuit main
module main (
  input  Data__D,
  input  Enable__E,
  input  CLK,
  input  J,
  input  K,
  output Q,
  output nQ,
  output Q_2,
  output nQ_2
);

  wire and_1_out, and_2_out, nand_1_out, nand_2_out, nand_3_out, not_1_out, or_1_out;

  D_Flip_Flop d_ff_1 ();  // open: clk, D, Q, Qn, preset, en, reset
  nand nand_1 (nand_1_out, Data__D, Data__D);
  J_K_Flip_Flop j_k_ff_1 ();  // open: J, clk, K, Q, Qn, preset, en, reset
  not not_1 (not_1_out, K);
  and and_1 (and_1_out, nQ_2, J);
  and and_2 (and_2_out, not_1_out, Q_2);
  nand nand_2 (nand_2_out, Data__D, Data__D);
  nand nand_3 (nand_3_out, Data__D, nand_1_out);
  D_Flip_Flop d_ff_2 (.clk(CLK), .D(or_1_out), .Q(Q_2), .Qn(nQ_2));  // open: preset, en, reset
  or or_1 (or_1_out, and_1_out, and_2_out);
  nand nand_4 (Q, nand_2_out, nQ);
  nand nand_5 (nQ, Q, nand_3_out);

  assign Enable__E = Data__D;

  // Notes on the sheet:
  //   FlipFlop (D)
  //   FlipFlop (JK) 
  //   [Componente 01] FlipFlop D e do Tipo JK
endmodule
