// Logisim project MemoriaROM_8BITS.circ as structural Verilog: 1 circuit, main circuit main
module main (
  input  A2,
  input  A1,
  input  A0,
  output out_4,
  output out_5,
  output out_6,
  output out_7,
  output out_8,
  output out_9,
  output out_10,
  output out_11
);

  wire and_1_out, and_2_out, and_3_out, and_4_out, and_5_out, and_6_out, and_7_out, and_8_out, not_1_out,
       not_2_out, not_3_out, not_4_out, not_5_out, not_6_out, not_7_out, not_8_out, not_9_out, not_10_out,
       not_11_out, not_12_out;

  not not_1 (not_1_out, A0);
  not not_2 (not_2_out, A1);
  not not_3 (not_3_out, A2);
  not not_4 (not_4_out, A2);
  not not_5 (not_5_out, A1);
  not not_6 (not_6_out, A0);
  not not_7 (not_7_out, A2);
  not not_8 (not_8_out, A2);
  not not_9 (not_9_out, A0);
  not not_10 (not_10_out, A1);
  not not_11 (not_11_out, A1);
  not not_12 (not_12_out, A0);
  and and_1 (and_1_out, not_1_out, not_2_out, not_3_out);
  and and_2 (and_2_out, not_4_out, not_5_out, A0);
  and and_3 (and_3_out, not_6_out, A1, not_7_out);
  and and_4 (and_4_out, not_8_out, A0, A1);
  and and_5 (and_5_out, not_9_out, not_10_out, A2);
  and and_6 (and_6_out, A0, not_11_out, A2);
  and and_7 (and_7_out, not_12_out, A1, A2);
  and and_8 (and_8_out, A0, A1, A2);
  or or_1 (out_4, and_5_out, and_6_out, and_7_out, and_8_out);
  or or_2 (out_5, and_7_out, and_8_out, and_4_out, and_3_out);
  buf or_3 (out_6, and_1_out);  // OR_Gate
  buf or_4 (out_7, and_4_out);  // OR_Gate
  buf or_5 (out_8, and_8_out);  // OR_Gate
  or or_6 (out_9, and_2_out, and_5_out, and_6_out, and_8_out);
  or or_7 (out_10, and_1_out, and_5_out, and_8_out);
  or or_8 (out_11, and_6_out, and_7_out, and_8_out, and_4_out, and_2_out);

  // Notes on the sheet:
  //   M0
  //   M1
  //   M2
  //   M3
  //   M4
  //   M5
  //   M6
  //   M7
  //   D7
  //   D6
  //   D5
  //   D4
  //   D3
  //   D2
  //   D1
  //   D0
  //   ENDEREÇO
  //   000 ->= 001 000 10
  //   001 ->= 000 001 01
  //   010 ->= 010 000 00
  //   011 -> 010 100 01
  //   100 ->= 100 001 10
  //   101 -> 100 001 01
  //   110 ->= 110 000 01
  //   111 ->= 110 011 11
  //   DATA
endmodule
