// Logisim project Detector101.circ as structural Verilog: 1 circuit, main circuit main
module main (
  input  [7:0] ENTRADA,
  output \SAÍDA 
);

  wire and_1_out, and_2_out, and_3_out, and_4_out, and_5_out, and_6_out, and_7_out, not_1_out, not_2_out,
       not_3_out, not_4_out, not_5_out, not_6_out, not_7_out;

  not not_1 (not_1_out, ENTRADA[1]);
  not not_2 (not_2_out, ENTRADA[2]);
  not not_3 (not_3_out, ENTRADA[3]);
  not not_4 (not_4_out, ENTRADA[4]);
  not not_5 (not_5_out, ENTRADA[5]);
  not not_6 (not_6_out, ENTRADA[6]);
  not not_7 (not_7_out, ENTRADA[7]);
  and and_1 (and_1_out, ENTRADA[0], not_1_out, ENTRADA[2]);
  and and_2 (and_2_out, ENTRADA[1], not_2_out, ENTRADA[3]);
  and and_3 (and_3_out, ENTRADA[2], not_3_out, ENTRADA[4]);
  and and_4 (and_4_out, ENTRADA[3], not_4_out, ENTRADA[5]);
  and and_5 (and_5_out, ENTRADA[4], not_5_out, ENTRADA[6]);
  and and_6 (and_6_out, ENTRADA[5], not_6_out, ENTRADA[7]);
  and and_7 (and_7_out, ENTRADA[6], not_7_out, ENTRADA[7]);
  or or_1 (\SAÍDA , and_1_out, and_2_out, and_3_out, and_4_out, and_5_out, and_6_out, and_7_out);

  // Notes on the sheet:
  //   1 - Para encontrado
  //   0 - Para não encontrado
endmodule
