// Logisim project ULA.circ as structural Verilog: 14 circuits, main circuit sum
module ULA (
  input  [7:0] in_1,
  input  [7:0] in_2,
  input  [3:0] Seletor,
  input  in_4,
  output [7:0] out_5,
  output out_6,
  output out_7
);

  wire [7:0] and_1_out, nand_1_out, nor_1_out, not_1_out, not_2_out, or_1_out, shiftl_1_s, shiftl_2_s,
       shiftr_1_s, shiftr_2_s, subtractor_1_out_3, sum_1_out_4, xor_1_out;

  assign not_1_out = ~in_1;  // NOT_Gate not_1, 8 bits wide
  assign not_2_out = ~in_2;  // NOT_Gate not_2, 8 bits wide
  assign and_1_out = in_1 & in_2;  // AND_Gate and_1, 8 bits wide
  assign or_1_out = in_1 | in_2;  // OR_Gate or_1, 8 bits wide
  assign nor_1_out = ~(in_1 | in_2);  // NOR_Gate nor_1, 8 bits wide
  assign nand_1_out = ~(in_1 & in_2);  // NAND_Gate nand_1, 8 bits wide
  assign xor_1_out = in_1 ^ in_2;  // XOR_Gate xor_1, 8 bits wide
  shiftL shiftl_1 (.A___B(in_1), .S(shiftl_1_s));
  shiftL shiftl_2 (.A___B(in_2), .S(shiftl_2_s));
  shiftR shiftr_1 (.A___B(in_1), .S(shiftr_1_s));
  shiftR shiftr_2 (.A___B(in_2), .S(shiftr_2_s));
  sum sum_1 (.out_4(sum_1_out_4), .A(in_1), .B(in_2), .CIN(in_4), .CARRYOUT(out_6));
  subtractor subtractor_1 (.out_3(subtractor_1_out_3), .A(in_1), .B(in_2), .COUT(out_7));
  MUX16x1x8 mux16x1x8_1 (
    .in_1(and_1_out), .in_2(or_1_out), .in_3(not_1_out), .in_4(not_2_out), .in_5(nor_1_out),
    .in_6(nand_1_out), .in_7(xor_1_out), .in_8(shiftl_1_s), .in_9(shiftl_2_s), .in_10(shiftr_1_s),
    .in_11(shiftr_2_s), .in_12(sum_1_out_4), .in_13(subtractor_1_out_3), .SELETOR(Seletor), .out_15(out_5));

  // Notes on the sheet:
  //   A
  //   B
endmodule

module sum (
  input  [7:0] A,
  input  [7:0] B,
  input  CIN,
  output [7:0] out_4,
  output CARRYOUT
);

  wire sum1bit_1_cout, sum1bit_2_cout, sum1bit_3_cout, sum1bit_4_cout, sum1bit_5_cout, sum1bit_6_cout,
       sum1bit_7_cout;

  sum1bit sum1bit_1 (.A(A[0]), .B(B[0]), .S(out_4[0]), .COUT(sum1bit_1_cout), .CIN(CIN));
  sum1bit sum1bit_2 (.A(A[1]), .B(B[1]), .S(out_4[1]), .COUT(sum1bit_2_cout), .CIN(sum1bit_1_cout));
  sum1bit sum1bit_3 (.A(A[2]), .B(B[2]), .S(out_4[2]), .COUT(sum1bit_3_cout), .CIN(sum1bit_2_cout));
  sum1bit sum1bit_4 (.A(A[3]), .B(B[3]), .S(out_4[3]), .COUT(sum1bit_4_cout), .CIN(sum1bit_3_cout));
  sum1bit sum1bit_5 (.A(A[4]), .B(B[4]), .S(out_4[4]), .COUT(sum1bit_5_cout), .CIN(sum1bit_4_cout));
  sum1bit sum1bit_6 (.A(A[5]), .B(B[5]), .S(out_4[5]), .COUT(sum1bit_6_cout), .CIN(sum1bit_5_cout));
  sum1bit sum1bit_7 (.A(A[6]), .B(B[6]), .S(out_4[6]), .COUT(sum1bit_7_cout), .CIN(sum1bit_6_cout));
  sum1bit sum1bit_8 (.A(A[7]), .B(B[7]), .S(out_4[7]), .COUT(CARRYOUT), .CIN(sum1bit_7_cout));

  // Notes on the sheet:
  //   S
endmodule

module subtractor (
  input  [7:0] A,
  input  [7:0] B,
  output [7:0] out_3,
  output COUT
);

  wire sub1bit_1_cout, sub1bit_2_cout, sub1bit_3_cout, sub1bit_4_cout, sub1bit_5_cout, sub1bit_6_cout,
       sub1bit_7_cout, sub1bit_8_cout;

  sub1bit sub1bit_1 (.A(A[0]), .B(B[0]), .S(out_3[0]), .COUT(sub1bit_1_cout));
  sub1bit sub1bit_2 (.A(A[1]), .B(B[1]), .S(out_3[1]), .COUT(sub1bit_2_cout));
  sub1bit sub1bit_3 (.A(A[2]), .B(B[2]), .S(out_3[2]), .COUT(sub1bit_3_cout));
  sub1bit sub1bit_4 (.A(A[3]), .B(B[3]), .S(out_3[3]), .COUT(sub1bit_4_cout));
  sub1bit sub1bit_5 (.A(A[4]), .B(B[4]), .S(out_3[4]), .COUT(sub1bit_5_cout));
  sub1bit sub1bit_6 (.A(A[5]), .B(B[5]), .S(out_3[5]), .COUT(sub1bit_6_cout));
  sub1bit sub1bit_7 (.A(A[6]), .B(B[6]), .S(out_3[6]), .COUT(sub1bit_7_cout));
  sub1bit sub1bit_8 (.A(A[7]), .B(B[7]), .S(out_3[7]), .COUT(sub1bit_8_cout));
  and and_1 (COUT, sub1bit_1_cout, sub1bit_2_cout, sub1bit_3_cout, sub1bit_4_cout, sub1bit_5_cout, sub1bit_6_cout, sub1bit_7_cout, sub1bit_8_cout);

  // Notes on the sheet:
  //   S
endmodule

module sum1bit (
  input  CIN,
  input  A,
  input  B,
  output S,
  output COUT
);

  wire and_1_out, and_2_out, and_3_out, xor_1_out;

  and and_1 (and_1_out, A, B);
  and and_2 (and_2_out, CIN, A);
  and and_3 (and_3_out, B, CIN);
  xor xor_1 (xor_1_out, A, B);
  or or_1 (COUT, and_1_out, and_2_out, and_3_out);
  xor xor_2 (S, xor_1_out, CIN);
endmodule

module sub1bit (
  input  A,
  input  B,
  output S,
  output COUT
);

  wire and_1_out, and_2_out, not_1_out, xor_1_out;

  not not_1 (not_1_out, B);
  xor xor_1 (xor_1_out, A, not_1_out);
  and and_1 (and_1_out, A, not_1_out);
  xor xor_2 (S, 1'b1, xor_1_out);
  and and_2 (and_2_out, 1'b1, xor_1_out);
  or or_1 (COUT, and_2_out, and_1_out);
endmodule

module shiftL (
  input  [7:0] A___B,
  output [7:0] S
);


  assign S = {A___B[5:0], 2'b00};
endmodule

module shiftR (
  input  [7:0] A___B,
  output [7:0] S
);


  assign S = {2'b00, A___B[7:2]};
endmodule

module NOT (
  input  [7:0] A___B,
  output [7:0] out_2
);

  not not_1 (out_2[0], A___B[0]);
  not not_2 (out_2[1], A___B[1]);
  not not_3 (out_2[2], A___B[2]);
  not not_4 (out_2[3], A___B[3]);
  not not_5 (out_2[4], A___B[4]);
  not not_6 (out_2[5], A___B[5]);
  not not_7 (out_2[6], A___B[6]);
  not not_8 (out_2[7], A___B[7]);

  // Notes on the sheet:
  //   CHOICE
  //   S
endmodule

module XOR (
  input  [7:0] A,
  input  [7:0] B,
  output [7:0] out_3
);

  xor xor_1 (out_3[0], A[0], B[0]);
  xor xor_2 (out_3[1], A[1], B[1]);
  xor xor_3 (out_3[2], A[2], B[2]);
  xor xor_4 (out_3[3], A[3], B[3]);
  xor xor_5 (out_3[4], A[4], B[4]);
  xor xor_6 (out_3[5], A[5], B[5]);
  xor xor_7 (out_3[6], A[6], B[6]);
  xor xor_8 (out_3[7], A[7], B[7]);

  // Notes on the sheet:
  //   S
endmodule

module MUX2x1 (
  input  A,
  input  B,
  input  in_3,
  output S
);

  wire and_1_out, and_2_out, not_1_out;

  not not_1 (not_1_out, in_3);
  and and_1 (and_1_out, A, not_1_out);
  and and_2 (and_2_out, B, in_3);
  or or_1 (S, and_1_out, and_2_out);

  // Notes on the sheet:
  //   SELETOR
endmodule

module MUX2X1X8 (
  input  [7:0] I0,
  input  [7:0] I1,
  input  in_3,
  output [7:0] out_4
);

  MUX2x1 mux2x1_1 (.A(I0[0]), .B(I1[0]), .S(out_4[0]), .in_3(in_3));
  MUX2x1 mux2x1_2 (.A(I0[1]), .B(I1[1]), .S(out_4[1]), .in_3(in_3));
  MUX2x1 mux2x1_3 (.A(I0[2]), .B(I1[2]), .S(out_4[2]), .in_3(in_3));
  MUX2x1 mux2x1_4 (.A(I0[3]), .B(I1[3]), .S(out_4[3]), .in_3(in_3));
  MUX2x1 mux2x1_5 (.A(I0[4]), .B(I1[4]), .S(out_4[4]), .in_3(in_3));
  MUX2x1 mux2x1_6 (.A(I0[5]), .B(I1[5]), .S(out_4[5]), .in_3(in_3));
  MUX2x1 mux2x1_7 (.A(I0[6]), .B(I1[6]), .S(out_4[6]), .in_3(in_3));
  MUX2x1 mux2x1_8 (.A(I0[7]), .B(I1[7]), .S(out_4[7]), .in_3(in_3));
endmodule

module MUX4X1X8 (
  input  [7:0] in_1,
  input  [7:0] in_2,
  input  [7:0] in_3,
  input  [7:0] in_4,
  input  [1:0] in_5,
  output [7:0] out_6
);

  wire [7:0] mux2x1x8_1_out_4, mux2x1x8_2_out_4;

  MUX2X1X8 mux2x1x8_1 (.out_4(mux2x1x8_1_out_4), .I0(in_1), .I1(in_2), .in_3(in_5[0]));
  MUX2X1X8 mux2x1x8_2 (.out_4(mux2x1x8_2_out_4), .I0(in_3), .I1(in_4), .in_3(in_5[0]));
  MUX2X1X8 mux2x1x8_3 (.out_4(out_6), .I0(mux2x1x8_1_out_4), .I1(mux2x1x8_2_out_4), .in_3(in_5[1]));

  // Notes on the sheet:
  //   I0
  //   I1
  //   I2
  //   I3
endmodule

module MUX8x1x8 (
  input  [7:0] in_1,
  input  [7:0] in_2,
  input  [7:0] in_3,
  input  [7:0] in_4,
  input  [7:0] in_5,
  input  [7:0] in_6,
  input  [7:0] in_7,
  input  [7:0] in_8,
  input  [2:0] SELETOR,
  output [7:0] out_10
);

  wire [7:0] mux4x1x8_1_out_6, mux4x1x8_2_out_6;

  MUX4X1X8 mux4x1x8_1 (
    .in_1(in_1), .in_2(in_2), .in_3(in_3), .in_4(in_4), .in_5(SELETOR[1:0]), .out_6(mux4x1x8_1_out_6));
  MUX4X1X8 mux4x1x8_2 (
    .in_1(in_5), .in_2(in_6), .in_3(in_7), .in_4(in_8), .in_5(SELETOR[1:0]), .out_6(mux4x1x8_2_out_6));
  MUX2X1X8 mux2x1x8_1 (.out_4(out_10), .I0(mux4x1x8_1_out_6), .I1(mux4x1x8_2_out_6), .in_3(SELETOR[2]));

  // Notes on the sheet:
  //   I0
  //   I1
  //   I2
  //   I3
  //   I4
  //   I5
  //   I6
  //   I7
  //   S
endmodule

module MUX16x1x8 (
  input  [7:0] in_1,
  input  [7:0] in_2,
  input  [7:0] in_3,
  input  [7:0] in_4,
  input  [7:0] in_5,
  input  [7:0] in_6,
  input  [7:0] in_7,
  input  [7:0] in_8,
  input  [7:0] in_9,
  input  [7:0] in_10,
  input  [7:0] in_11,
  input  [7:0] in_12,
  input  [7:0] in_13,
  input  [3:0] SELETOR,
  output [7:0] out_15
);

  wire [7:0] mux8x1x8_1_out_10, mux8x1x8_2_out_10;

  MUX8x1x8 mux8x1x8_1 (
    .in_1(in_1), .in_2(in_2), .in_3(in_3), .in_4(in_4), .in_5(in_5), .in_6(in_6), .in_7(in_7), .in_8(in_8),
    .SELETOR(SELETOR[2:0]), .out_10(mux8x1x8_1_out_10));
  MUX8x1x8 mux8x1x8_2 (
    .in_1(in_9), .in_2(in_10), .in_3(in_11), .in_4(in_12), .in_5(in_13), .in_6({8{1'b0}}), .in_7({8{1'b0}}),
    .in_8({8{1'b0}}), .SELETOR(SELETOR[2:0]), .out_10(mux8x1x8_2_out_10));
  MUX2X1X8 mux2x1x8_1 (.out_4(out_15), .I0(mux8x1x8_1_out_10), .I1(mux8x1x8_2_out_10), .in_3(SELETOR[3]));

  // Notes on the sheet:
  //   I0
  //   I1
  //   I2
  //   I3
  //   I4
  //   I5
  //   I6
  //   I7
  //   I8
  //   I9
  //   I10
  //   I11
  //   I2
  //   S
endmodule
