// Logisim project IdentificardorDePrimo.circ as structural Verilog: 1 circuit, main circuit main
module main (
  input  [3:0] ENTRADA,
  output \SAIDA__1___PRIMO____0___NÃO_PRIMO 
);

  wire and_1_out, and_2_out, and_3_out, and_4_out, not_1_out, not_2_out, not_3_out, not_4_out, not_5_out;

  not not_1 (not_1_out, ENTRADA[3]);
  not not_2 (not_2_out, ENTRADA[2]);
  not not_3 (not_3_out, ENTRADA[2]);
  not not_4 (not_4_out, ENTRADA[3]);
  not not_5 (not_5_out, ENTRADA[1]);
  and and_1 (and_1_out, not_1_out, not_2_out, ENTRADA[1]);
  and and_2 (and_2_out, not_3_out, ENTRADA[1], ENTRADA[0]);
  and and_3 (and_3_out, not_4_out, ENTRADA[2], ENTRADA[0]);
  and and_4 (and_4_out, ENTRADA[2], not_5_out, ENTRADA[0]);
  or or_1 (\SAIDA__1___PRIMO____0___NÃO_PRIMO , and_1_out, and_2_out, and_3_out, and_4_out);
endmodule
